# Fritzing sketch audio_connections_diagram (saved by Fritzing 0.9.9b)
breadboards: 1

parts:
  DFPlayer_Mini2 = DFPlayer MINI [package="DIP (Dual Inline) [THT]"]
  SP2 = SPEAKER [package=pcb_mount_speaker]
  Composant5 = Arduino Mega 2560 (Rev3)
  Composant6 = Adafruit USB Type C Breakout [part_number=4090]
  Mod1 = Passive Buzzer

nets:
  VCC: DFPlayer_Mini2.VCC, Composant5.3V3
  N1: DFPlayer_Mini2.RX, Composant5.D46
  N2: DFPlayer_Mini2.TX, Composant5.D12_PWM
  N3: DFPlayer_Mini2.SPK1, SP2.+
  N4: DFPlayer_Mini2.GND#6, Composant6.GND, Mod1.-
  N5: DFPlayer_Mini2.SPK2, SP2.-
  N6: Composant5.D13_PWM, Mod1.S
  GND: Composant5.GND, Composant5.VIN, Composant6.VBUS

custom parts:
  DFPlayer MINI: MP3 module by DFRobot.com for playing Music from an SD-Card. Supports WAV and MP3 files.
  Adafruit USB Type C Breakout: Adafruit breakout board for USB Type C socket.
