# Fritzing sketch inputs_connections_diagram (saved by Fritzing 0.9.9b)
breadboards: 1

parts:
  Composant2 = Arduino Mega ADK (Rev3)
  KEYPAD2 = Membrane Matrix Keypad
  S1 = Pushbutton [package="[SMD]"]
  S2 = Pushbutton [package="[SMD]"]
  S3 = Pushbutton [package="[SMD]"]
  S4 = Pushbutton [package="[SMD]"]
  R1 = Resistor [tolerance=±5% resistance=1k package="1206 [SMD]"]
  R2 = Resistor [tolerance=±5% resistance=1k package="1206 [SMD]"]
  R3 = Resistor [tolerance=±5% resistance=1k package="1206 [SMD]"]
  R4 = Resistor [tolerance=±5% resistance=1k package="1206 [SMD]"]
  Composant5 = Adafruit USB Type C Breakout [part_number=4090]

nets:
  GND: Composant2.GND, R1.Pin_1, R2.Pin_1, R3.Pin_1, R4.Pin_1, Composant5.GND
  N1: Composant2.D11_PWM, KEYPAD2.1
  N2: Composant2.D10_PWM, KEYPAD2.2
  N3: Composant2.D9_PWM, KEYPAD2.3
  N4: Composant2.D8_PWM, KEYPAD2.4
  N5: Composant2.D3_PWM, KEYPAD2.7
  N6: Composant2.D4_PWM, KEYPAD2.6
  N7: Composant2.D5_PWM, KEYPAD2.5
  N8: Composant2.D22, S2.Pin_1, S2.Pin_2, R2.Pin_0
  N9: Composant2.D23, S4.Pin_1, S4.Pin_2, R1.Pin_0
  N10: Composant2.D24, S1.Pin_1, S1.Pin_2, R3.Pin_0
  N11: Composant2.D25, S3.Pin_1, S3.Pin_2, R4.Pin_0
  N12: S1.Pin_3, S1.Pin_4
  N13: S2.Pin_3, S2.Pin_4, S3.Pin_3, S3.Pin_4, S4.Pin_3, S4.Pin_4, Composant5.VBUS

custom parts:
  Membrane Matrix Keypad: Membrane Matrix 3x4 Keypad
  Adafruit USB Type C Breakout: Adafruit breakout board for USB Type C socket.
