# Fritzing sketch LEDs_connections_diagram (saved by Fritzing 0.9.9b)
breadboards: 1

parts:
  Composant6 = Arduino Mega ADK (Rev3)
  Composant7 = Adafruit USB Type C Breakout [part_number=4090]
  LED4 = LEDs [package=led10mm]
  LED5 = LEDs [package=led10mm]
  LED6 = LEDs [package=led10mm]
  R4 = Resistor [tolerance=±5% resistance=220 package="2010 [SMD]"]
  R5 = Resistor [tolerance=±5% resistance=220 package="2010 [SMD]"]
  R6 = Resistor [tolerance=±5% resistance=220 package="2010 [SMD]"]
  LED7 = LED - 5mm [color="Red (633nm)" current=0.030 package="5 mm [THT]"]
  LED8 = LED - 5mm [color="Red (633nm)" current=0.030 package="5 mm [THT]"]
  LED9 = LED - 5mm [color="Green (560nm)" current=0.030 package="5 mm [THT]"]
  R7 = Resistor [tolerance=±5% resistance=220 package="1206 [SMD]"]
  R8 = Resistor [tolerance=±5% resistance=220 package="1206 [SMD]"]
  R9 = Resistor [tolerance=±5% resistance=220 package="1206 [SMD]"]
  M1 = Grove Electromagnet

nets:
  GND: Composant6.GND, Composant7.GND, R6.Pin_1, R8.Pin_0, R9.Pin_0, M1.GND
  VIN: Composant6.VIN, Composant7.VBUS, M1.VCC
  N1: Composant6.D7_PWM, M1.SIG
  N2: Composant6.D26, LED5.A
  N3: Composant6.D27, LED4.A
  N4: Composant6.D28, LED6.A
  N5: Composant6.D30, LED8.cathode, R9.Pin_1
  N6: Composant6.D31, LED9.anode
  N7: Composant6.D35, LED7.anode
  N8: LED4.C, R6.Pin_0
  N9: LED5.C, R4.Pin_0
  N10: LED6.C, R5.Pin_0
  N11: LED7.cathode, R7.Pin_1
  N12: LED9.cathode, R7.Pin_0, R8.Pin_1

custom parts:
  Adafruit USB Type C Breakout: Adafruit breakout board for USB Type C socket.
  Grove Electromagnet: Grove Electromagnet.
